# Fritzing sketch larson scanner wiring (saved by Fritzing 0.9.3b)
breadboards: 1

parts:
  R1 = Resistor [tolerance=±5% resistance=220 package=THT]
  R2 = Resistor [tolerance=±5% resistance=220 package=THT]
  R3 = Resistor [tolerance=±5% resistance=220 package=THT]
  R4 = Resistor [tolerance=±5% resistance=220 package=THT]
  R5 = Resistor [tolerance=±5% resistance=220 package=THT]
  R6 = Resistor [tolerance=±5% resistance=220 package=THT]
  LED2 = smd LED [color="Red (633nm)" package="1206 [SMD]"]
  LED3 = smd LED [color="Red (633nm)" package="1206 [SMD]"]
  LED4 = smd LED [color="Red (633nm)" package="1206 [SMD]"]
  LED5 = smd LED [color="Red (633nm)" package="1206 [SMD]"]
  LED6 = smd LED [color="Red (633nm)" package="1206 [SMD]"]
  LED7 = smd LED [color="Red (633nm)" package="1206 [SMD]"]
  Part1 = Arduino Uno (Rev3)

nets:
  N1: R1.Pin_0, LED3.anode
  N2: R1.Pin_1, Part1.D9_PWM
  N3: R2.Pin_0, LED2.anode
  N4: R2.Pin_1, Part1.D8
  N5: R3.Pin_0, LED4.anode
  N6: R3.Pin_1, Part1.D7
  N7: R4.Pin_0, LED5.anode
  N8: R4.Pin_1, Part1.D6_PWM
  N9: R5.Pin_0, LED6.anode
  N10: R5.Pin_1, Part1.D5_PWM
  N11: R6.Pin_0, LED7.anode
  N12: R6.Pin_1, Part1.D4
  N13: LED2.cathode, LED3.cathode, LED4.cathode, LED5.cathode, LED6.cathode, LED7.cathode, Part1.GND
